# Fritzing sketch arduinorfid (saved by Fritzing 0.8.7b)

parts:
  Part1 = Arduino Uno (Rev3)
  RFID1 = RFID Reader

nets:
  N1: Part1.D13/SCK, RFID1.RES
  N2: Part1.D0/RX, RFID1.D0
  5V: Part1.5V, RFID1.+5V
  GND: Part1.GND, RFID1.GND
