# Fritzing sketch motorcontrol (saved by Fritzing 0.8.7b)

parts:
  RaspberryPi1 = Raspberry Pi Model B
  Part1 = EasyDriver_v44
  R1 = Resistor [tolerance=±5% resistance=1k package=THT]
  M1 = Stepper Motor - Bipolar
  R2 = Resistor [tolerance=±5% resistance=1k package=THT]

nets:
  GND: RaspberryPi1.GND, Part1.GND, Part1.MS1, Part1.MS2, R1.Pin_1, R2.Pin_1
  N1: RaspberryPi1.#23, Part1.STEP, R2.Pin_0
  N2: RaspberryPi1.#24, Part1.DIR, R1.Pin_0
  N3: Part1.OUT2A, M1.A
  N4: Part1.OUT2B, M1.C
  N5: Part1.OUT1A, M1.B
  N6: Part1.OUT1B, M1.D

notes:
  12 Volts

custom parts:
  Raspberry Pi Model B: Raspberry Pi (Model B)
