# Fritzing sketch motorcontrolandrfid (saved by Fritzing 0.8.7b)

parts:
  Part1 = EasyDriver_v44
  R1 = Resistor [tolerance=±5% resistance=1k package=THT]
  R2 = Resistor [tolerance=±5% resistance=1k package=THT]
  M1 = Stepper Motor - Bipolar
  RFID1 = RFID Reader
  R3 = Resistor [tolerance=±5% resistance=200 package=THT]
  R4 = Resistor [tolerance=±5% resistance=390 package=THT]
  R5 = Resistor [tolerance=±5% resistance=220 package=THT]
  R6 = Resistor [tolerance=±5% resistance=220 package=THT]
  LED1 = LED - 5mm [color="Green (570nm)" package="5 mm [THT]"]
  LED2 = LED - 5mm [color="Red (633nm)" package="5 mm [THT]"]
  RaspberryPi1 = Raspberry Pi Model B

nets:
  N1: Part1.GND, Part1.MS2
  N2: Part1.STEP, R1.Pin_1, RaspberryPi1.#23
  N3: Part1.DIR, R2.Pin_1, RaspberryPi1.#24
  N4: Part1.OUT2A, M1.A
  N5: Part1.OUT2B, M1.C
  N6: Part1.OUT1A, M1.B
  N7: Part1.OUT1B, M1.D
  N8: RFID1.D0, R3.Pin_0
  +5V: RFID1.+5V, RaspberryPi1.5V
  N9: R3.Pin_1, R4.Pin_0, RaspberryPi1.RXD
  N10: R5.Pin_0, RaspberryPi1.#17
  N11: R5.Pin_1, LED1.anode
  N12: R6.Pin_0, RaspberryPi1.#4
  N13: R6.Pin_1, LED2.anode

notes:
  12 Volts
  220Ω

custom parts:
  Raspberry Pi Model B: Raspberry Pi (Model B)
