# Fritzing sketch motorcontrolandrfids_schem (saved by Fritzing 0.8.7b)

parts:
  M1 = Stepper Motor - Bipolar
  Part1 = EasyDriver_v44
  RFID1 = RFID Reader
  RaspberryPi1 = Raspberry Pi Model B
  R1 = Resistor [tolerance=±5% resistance=1k package=THT]
  R2 = Resistor [tolerance=±5% resistance=1k package=THT]
  LED1 = LED - 5mm [color="Red (633nm)" package="5 mm [THT]"]
  LED2 = LED - 5mm [color="Green (570nm)" package="5 mm [THT]"]
  R3 = Resistor [tolerance=±5% resistance=220 package=THT]
  R4 = Resistor [tolerance=±5% resistance=220 package=THT]
  R5 = Resistor [tolerance=±5% resistance=200 package=THT]
  R6 = Resistor [tolerance=±5% resistance=390 package=THT]

nets:
  N1: M1.A, Part1.OUT2A
  N2: M1.C, Part1.OUT2B
  N3: M1.B, Part1.OUT1A
  N4: M1.D, Part1.OUT1B
  GND: Part1.GND, Part1.MS1, Part1.MS2, RFID1.GND, RFID1.+/-, RaspberryPi1.GND, R1.Pin_0, R2.Pin_0, LED1.cathode, LED2.cathode, R6.Pin_1
  N5: Part1.STEP, RaspberryPi1.#23, R2.Pin_1
  N6: Part1.DIR, RaspberryPi1.#24, R1.Pin_1
  N7: Part1.ENABLE, RaspberryPi1.#25
  N8: RFID1.D0, R5.Pin_1
  +5V: RFID1.+5V, RaspberryPi1.5V
  N9: RaspberryPi1.#4, R3.Pin_1
  N10: RaspberryPi1.RXD, R5.Pin_0, R6.Pin_0
  N11: RaspberryPi1.#17, R4.Pin_1
  N12: LED1.anode, R3.Pin_0
  N13: LED2.anode, R4.Pin_0

custom parts:
  Raspberry Pi Model B: Raspberry Pi (Model B)
